# Fritzing sketch boardlayout (saved by Fritzing 0.8.7b)
circuit board: 7.69286cm x 7.12295cm
breadboards: 1

parts:
  LED7 = LED - 5mm [color="Red (633nm)" package="5 mm [THT]"]
  LED6 = LED - 5mm [color="Red (633nm)" package="5 mm [THT]"]
  LED5 = LED - 5mm [color="Red (633nm)" package="5 mm [THT]"]
  LED4 = LED - 5mm [color="Red (633nm)" package="5 mm [THT]"]
  LED2 = LED - 5mm [color="Red (633nm)" package="5 mm [THT]"]
  LED3 = LED - 5mm [color="Red (633nm)" package="5 mm [THT]"]
  LED1 = LED - 5mm [color="Red (633nm)" package="5 mm [THT]"]
  Nano_V3_0 = Arduino Nano (Rev3.0)
  IR_LED = LED - 5mm [color="Red (633nm)" package="5 mm [THT]"]

nets:
  N1: LED7.cathode, LED6.cathode, LED5.cathode, LED4.cathode, LED2.cathode, LED3.cathode, LED1.cathode, Nano_V3_0.GND, IR_LED.cathode
  N2: LED7.anode, Nano_V3_0.D6
  N3: LED6.anode, Nano_V3_0.D5
  N4: LED5.anode, Nano_V3_0.D4
  N5: LED4.anode, Nano_V3_0.D2
  N6: LED2.anode, Nano_V3_0.A5
  N7: LED3.anode, Nano_V3_0.A4
  N8: LED1.anode, Nano_V3_0.A3
  N9: Nano_V3_0.D3, IR_LED.anode

notes:
  D12
  D13
  VIN
  TX1
  GND
